# Fritzing sketch PIR_test (saved by Fritzing 0.9.2b)
breadboards: 1

parts:
  PIR1 = PIR sensor
  Composant1 = Arduino Uno (Rev3)
  LED1 = LED - 5mm [color="Red (633nm)" package="5 mm [THT]"]
  R1 = Resistor [tolerance=±5% resistance=220 package=THT]

nets:
  VDD: PIR1.VDD, Composant1.5V
  N1: PIR1.SIG, LED1.cathode
  GND: PIR1.GND, Composant1.GND, R1.Pin_1
  N2: LED1.anode, R1.Pin_0
